// Logisim project CSE332.6-2012673642-Anik-Pal.circ as structural Verilog: 11 circuits, main circuit main
// D flipflop
module main (
);

  wire and_1_out, and_2_out, and_3_out, and_4_out, and_5_out, clock_1_out, j_k_ff_1_q, j_k_ff_2_q,
       j_k_ff_3_q, not_1_out, not_2_out, not_3_out, or_1_out, or_2_out, or_3_out, or_4_out, or_5_out,
       or_6_out, or_7_out, or_8_out;

  not not_1 (not_1_out, j_k_ff_3_q);
  not not_2 (not_2_out, j_k_ff_2_q);
  not not_3 (not_3_out, j_k_ff_1_q);
  or or_1 (or_1_out, j_k_ff_3_q, j_k_ff_2_q, not_3_out);
  or or_2 (or_2_out, j_k_ff_3_q, not_3_out);
  or or_3 (or_3_out, j_k_ff_3_q, j_k_ff_2_q);
  or or_4 (or_4_out, j_k_ff_3_q, j_k_ff_1_q);
  or or_5 (or_5_out, j_k_ff_2_q, j_k_ff_1_q);
  and and_1 (and_1_out, not_1_out, not_1_out);
  or or_6 (or_6_out, not_2_out, j_k_ff_1_q);
  or or_7 (or_7_out, j_k_ff_3_q, j_k_ff_2_q, not_3_out);
  or or_8 (or_8_out, not_1_out, j_k_ff_1_q);
  and and_2 (and_2_out, or_3_out, or_4_out);
  and and_3 (and_3_out, not_1_out, or_6_out);
  and and_4 (and_4_out, or_7_out, or_8_out);
  _7_Segment_Display u_7_segment_display_1 (
    .g(and_4_out), .f(and_3_out), .a(or_1_out), .b(or_2_out), .e(and_1_out), .d(or_5_out), .c(and_2_out));  // open: dp
  Clock clock_1 (.out(clock_1_out));
  J_K_Flip_Flop j_k_ff_1 (.J(1'b1), .clk(clock_1_out), .K(1'b1), .Q(j_k_ff_1_q));  // open: Qn, preset, en, reset
  J_K_Flip_Flop j_k_ff_2 (
    .J(j_k_ff_1_q), .clk(clock_1_out), .K(j_k_ff_1_q), .Q(j_k_ff_2_q));  // open: Qn, preset, en, reset
  and and_5 (and_5_out, j_k_ff_1_q, j_k_ff_2_q);
  J_K_Flip_Flop j_k_ff_3 (
    .J(and_5_out), .clk(clock_1_out), .K(and_5_out), .Q(j_k_ff_3_q));  // open: Qn, preset, en, reset

  // Notes on the sheet:
  //   A
  //   B
  //   C
  //   a
  //   c
  //   d
  //   e
  //   f
  //   g
  //   Counter
endmodule

module Generalized_Equation__SOP (
  input  A,
  input  B,
  input  C
);

  wire and_1_out, and_2_out, and_3_out, and_4_out, and_5_out, and_6_out, and_7_out, and_8_out, and_9_out,
       and_10_out, and_11_out, and_12_out, and_13_out, and_14_out, and_15_out, and_16_out, and_17_out,
       and_18_out, and_19_out, and_20_out, and_21_out, and_22_out, and_23_out, and_24_out, and_25_out,
       and_26_out, and_27_out, not_1_out, not_2_out, not_3_out, or_1_out, or_2_out, or_3_out, or_4_out,
       or_5_out, or_6_out, or_7_out, or_8_out, or_9_out, or_10_out, or_11_out, or_12_out;

  not not_1 (not_1_out, A);
  not not_2 (not_2_out, B);
  not not_3 (not_3_out, C);
  and and_1 (and_1_out, not_1_out, not_2_out, not_3_out);
  and and_2 (and_2_out, not_1_out, B, not_3_out);
  and and_3 (and_3_out, not_1_out, B, C);
  and and_4 (and_4_out, A, not_2_out, not_3_out);
  and and_5 (and_5_out, A, not_2_out, C);
  and and_6 (and_6_out, not_1_out, not_2_out, not_3_out);
  and and_7 (and_7_out, not_1_out, B, not_3_out);
  and and_8 (and_8_out, A, not_2_out, not_3_out);
  and and_9 (and_9_out, A, not_2_out, C);
  and and_10 (and_10_out, not_1_out, B, C);
  and and_11 (and_11_out, A, not_2_out, not_3_out);
  and and_12 (and_12_out, A, not_2_out, C);
  and and_13 (and_13_out, not_1_out, not_2_out, C);
  and and_14 (and_14_out, not_1_out, B, not_3_out);
  and and_15 (and_15_out, not_1_out, B, C);
  and and_16 (and_16_out, A, not_2_out, C);
  and and_17 (and_17_out, not_1_out, not_2_out, not_3_out);
  and and_18 (and_18_out, not_1_out, not_2_out, C);
  and and_19 (and_19_out, not_1_out, B, not_3_out);
  and and_20 (and_20_out, not_1_out, B, C);
  and and_21 (and_21_out, not_1_out, not_2_out, not_3_out);
  and and_22 (and_22_out, not_1_out, not_2_out, C);
  and and_23 (and_23_out, not_1_out, B, C);
  and and_24 (and_24_out, not_1_out, not_2_out, not_3_out);
  and and_25 (and_25_out, not_1_out, B, not_3_out);
  and and_26 (and_26_out, not_1_out, B, C);
  and and_27 (and_27_out, A, not_2_out, C);
  or or_1 (or_1_out, and_6_out, and_7_out, and_8_out);
  or or_2 (or_2_out, and_1_out, and_2_out, and_3_out);
  or or_3 (or_3_out, or_2_out, and_4_out, and_5_out);
  or or_4 (or_4_out, or_1_out, and_9_out);
  or or_5 (or_5_out, and_10_out, and_11_out, and_12_out);
  or or_6 (or_6_out, and_13_out, and_14_out, and_15_out);
  or or_7 (or_7_out, and_17_out, and_18_out, and_19_out);
  or or_8 (or_8_out, and_21_out, and_22_out, and_23_out);
  or or_9 (or_9_out, and_24_out, and_25_out, and_26_out);
  or or_10 (or_10_out, or_6_out, and_16_out);
  or or_11 (or_11_out, or_7_out, and_20_out);
  or or_12 (or_12_out, or_9_out, and_27_out);
  _7_Segment_Display u_7_segment_display_1 (
    .g(or_12_out), .f(or_8_out), .a(or_3_out), .b(or_4_out), .e(or_11_out), .d(or_10_out), .c(or_5_out));  // open: dp

  // Notes on the sheet:
  //   a
  //   b
  //   c
  //   d
  //   e
  //   f
  //   Generalized  Equation  (SOP)
  //   g
endmodule

module Generalized_Equation__POS (
  input  A,
  input  B,
  input  C
);

  wire and_1_out, and_2_out, and_3_out, and_4_out, and_5_out, and_6_out, not_1_out, not_2_out, not_3_out,
       or_1_out, or_2_out, or_3_out, or_4_out, or_5_out, or_6_out, or_7_out, or_8_out, or_9_out, or_10_out,
       or_11_out, or_12_out, or_13_out, or_14_out, or_15_out;

  not not_1 (not_1_out, A);
  not not_2 (not_2_out, B);
  not not_3 (not_3_out, C);
  or or_1 (or_1_out, A, B, not_3_out);
  or or_2 (or_2_out, A, B, not_3_out);
  or or_3 (or_3_out, A, not_2_out, not_3_out);
  or or_4 (or_4_out, A, B, C);
  or or_5 (or_5_out, A, B, not_3_out);
  or or_6 (or_6_out, A, not_2_out, C);
  or or_7 (or_7_out, A, B, C);
  or or_8 (or_8_out, not_1_out, B, C);
  or or_9 (or_9_out, not_1_out, B, C);
  or or_10 (or_10_out, not_1_out, B, not_3_out);
  or or_11 (or_11_out, A, not_2_out, C);
  or or_12 (or_12_out, not_1_out, B, C);
  or or_13 (or_13_out, not_1_out, B, not_3_out);
  or or_14 (or_14_out, A, B, not_3_out);
  or or_15 (or_15_out, not_1_out, B, C);
  and and_1 (and_1_out, or_2_out, or_3_out);
  and and_2 (and_2_out, or_4_out, or_5_out, or_6_out);
  and and_3 (and_3_out, or_7_out, or_8_out);
  and and_4 (and_4_out, or_9_out, or_10_out);
  and and_5 (and_5_out, or_11_out, or_12_out, or_13_out);
  and and_6 (and_6_out, or_14_out, or_15_out);
  _7_Segment_Display u_7_segment_display_1 (
    .g(and_6_out), .f(and_5_out), .a(or_1_out), .b(and_1_out), .e(and_4_out), .d(and_3_out), .c(and_2_out));  // open: dp

  // Notes on the sheet:
  //   a
  //   b
  //   c
  //   d
  //   e
  //   f
  //   g
  //   Generalized  Equation (POS)
endmodule

// A
module Simplified_Equation__SOP (
  input  A,
  input  B,
  input  C
);

  wire and_1_out, and_2_out, and_3_out, and_4_out, and_5_out, not_1_out, not_2_out, not_3_out, or_1_out,
       or_2_out, or_3_out, or_4_out, or_5_out, or_6_out, or_7_out;

  not not_1 (not_1_out, A);
  not not_2 (not_2_out, B);
  not not_3 (not_3_out, C);
  or or_1 (or_1_out, A, B, not_3_out);
  or or_2 (or_2_out, A, not_3_out);
  and and_1 (and_1_out, B, C);
  or or_3 (or_3_out, B, C);
  or or_4 (or_4_out, not_1_out, not_1_out);
  and and_2 (and_2_out, not_1_out, not_2_out);
  and and_3 (and_3_out, B, C);
  and and_4 (and_4_out, not_1_out, not_3_out);
  and and_5 (and_5_out, A, C);
  or or_5 (or_5_out, A, and_1_out);
  or or_6 (or_6_out, and_2_out, and_3_out);
  or or_7 (or_7_out, and_4_out, and_5_out, B);
  _7_Segment_Display u_7_segment_display_1 (
    .g(or_7_out), .f(or_6_out), .a(or_1_out), .b(or_2_out), .e(or_4_out), .d(or_3_out), .c(or_5_out));  // open: dp

  // Notes on the sheet:
  //   Simplified  Equation (SOP)
  //   a
  //   b
  //   d
  //   e
  //   c
  //   f
  //   g
endmodule

module Simplified_Equation__POS (
  input  A,
  input  B,
  input  C
);

  wire and_1_out, and_2_out, and_3_out, and_4_out, not_1_out, not_2_out, not_3_out, or_1_out, or_2_out,
       or_3_out, or_4_out, or_5_out, or_6_out, or_7_out, or_8_out;

  not not_1 (not_1_out, A);
  not not_2 (not_2_out, B);
  not not_3 (not_3_out, C);
  or or_1 (or_1_out, A, B, not_3_out);
  or or_2 (or_2_out, A, not_3_out);
  or or_3 (or_3_out, A, B);
  or or_4 (or_4_out, A, C);
  or or_5 (or_5_out, B, C);
  and and_1 (and_1_out, not_1_out, not_1_out);
  or or_6 (or_6_out, not_2_out, C);
  or or_7 (or_7_out, A, B, not_3_out);
  or or_8 (or_8_out, not_1_out, C);
  and and_2 (and_2_out, or_3_out, or_4_out);
  and and_3 (and_3_out, not_1_out, or_6_out);
  and and_4 (and_4_out, or_7_out, or_8_out);
  _7_Segment_Display u_7_segment_display_1 (
    .g(and_4_out), .f(and_3_out), .a(or_1_out), .b(or_2_out), .e(and_1_out), .d(or_5_out), .c(and_2_out));  // open: dp

  // Notes on the sheet:
  //   Simplified  Equation (POS)
  //   a
  //   c
  //   d
  //   e
  //   f
  //   g
endmodule

module NAND_Gate__SOP (
  input  A,
  input  B,
  input  C
);

  wire nand_1_out, nand_2_out, nand_3_out, nand_4_out, nand_5_out, nand_6_out, nand_7_out, nand_8_out,
       nand_9_out, nand_10_out, nand_11_out, nand_12_out, nand_13_out, nand_14_out, nand_15_out, nand_16_out,
       nand_17_out, nand_18_out, nand_19_out, nand_20_out, nand_21_out, nand_22_out, nand_23_out;

  nand nand_1 (nand_1_out, A, A);
  nand nand_2 (nand_2_out, A, A);
  nand nand_3 (nand_3_out, B, C);
  nand nand_4 (nand_4_out, B, B);
  nand nand_5 (nand_5_out, C, C);
  nand nand_6 (nand_6_out, A, A);
  nand nand_7 (nand_7_out, A, A);
  nand nand_8 (nand_8_out, B, B);
  nand nand_9 (nand_9_out, B, C);
  nand nand_10 (nand_10_out, A, C);
  nand nand_11 (nand_11_out, A, A);
  nand nand_12 (nand_12_out, C, C);
  nand nand_13 (nand_13_out, B, B);
  nand nand_14 (nand_14_out, A, A);
  nand nand_15 (nand_15_out, B, B);
  nand nand_16 (nand_16_out, nand_14_out, nand_15_out, C);
  nand nand_17 (nand_17_out, nand_1_out, C);
  nand nand_18 (nand_18_out, nand_2_out, nand_3_out);
  nand nand_19 (nand_19_out, nand_4_out, nand_5_out);
  nand nand_20 (nand_20_out, nand_7_out, nand_8_out);
  nand nand_21 (nand_21_out, nand_11_out, nand_12_out);
  nand nand_22 (nand_22_out, nand_20_out, nand_9_out);
  nand nand_23 (nand_23_out, nand_10_out, nand_13_out, nand_21_out);
  _7_Segment_Display u_7_segment_display_1 (
    .g(nand_23_out), .f(nand_22_out), .a(nand_16_out), .b(nand_17_out), .e(nand_6_out), .d(nand_19_out),
    .c(nand_18_out));  // open: dp

  // Notes on the sheet:
  //   e
  //   f
  //   a
  //   b
  //   c
  //   d
  //   NAND  (SOP)
  //   g
endmodule

module NOR_gate__POS (
  input  A,
  input  B,
  input  C
);

  wire nor_1_out, nor_2_out, nor_3_out, nor_4_out, nor_5_out, nor_6_out, nor_7_out, nor_8_out, nor_9_out,
       nor_10_out, nor_11_out, nor_12_out, nor_13_out, nor_14_out, nor_15_out, nor_16_out, nor_17_out,
       nor_18_out, nor_19_out, nor_20_out;

  nor nor_1 (nor_1_out, C, C);
  nor nor_2 (nor_2_out, C, C);
  nor nor_3 (nor_3_out, A, B);
  nor nor_4 (nor_4_out, A, C);
  nor nor_5 (nor_5_out, B, C);
  nor nor_6 (nor_6_out, A, A);
  nor nor_7 (nor_7_out, B, B);
  nor nor_8 (nor_8_out, A, A);
  nor nor_9 (nor_9_out, C, C);
  nor nor_10 (nor_10_out, A, nor_2_out);
  nor nor_11 (nor_11_out, nor_3_out, nor_4_out);
  nor nor_12 (nor_12_out, nor_5_out, nor_5_out);
  nor nor_13 (nor_13_out, nor_8_out, C);
  nor nor_14 (nor_14_out, A, B, nor_9_out);
  nor nor_15 (nor_15_out, A, B, nor_1_out);
  nor nor_16 (nor_16_out, nor_7_out, C);
  nor nor_17 (nor_17_out, nor_15_out, nor_15_out);
  nor nor_18 (nor_18_out, nor_10_out, nor_10_out);
  nor nor_19 (nor_19_out, A, nor_16_out);
  nor nor_20 (nor_20_out, nor_13_out, nor_14_out);
  _7_Segment_Display u_7_segment_display_1 (
    .g(nor_20_out), .f(nor_19_out), .a(nor_17_out), .b(nor_18_out), .e(nor_6_out), .d(nor_12_out),
    .c(nor_11_out));  // open: dp

  // Notes on the sheet:
  //   e
  //   c
  //   d
  //   b
  //   g
  //   a
  //   f
  //   NOR ( POS)
endmodule

module _4_1_MUX (
  input  I0,
  input  I1,
  input  I2,
  input  I3,
  input  S1,
  input  S0,
  output F
);

  wire and_1_out, and_2_out, and_3_out, and_4_out, not_1_out, not_2_out, or_1_out, or_2_out;

  not not_1 (not_1_out, S1);
  not not_2 (not_2_out, S0);
  and and_1 (and_1_out, I0, not_1_out, not_2_out);
  and and_2 (and_2_out, I1, not_1_out, S0);
  and and_3 (and_3_out, I2, S1, not_2_out);
  and and_4 (and_4_out, I3, S1, S0);
  or or_1 (or_1_out, and_1_out, and_2_out);
  or or_2 (or_2_out, and_3_out, and_4_out);
  or or_3 (F, or_1_out, or_2_out);
endmodule

module _7_segment_decoder (
  input  [2:0] ABC
);

  wire c_out, decoder_1_out0, decoder_1_out1, decoder_1_out2, decoder_1_out3, decoder_1_out4, decoder_1_out5,
       decoder_1_out6, decoder_1_out7, f_out, or_1_out, or_2_out, or_3_out, or_4_out, or_5_out, or_6_out,
       or_7_out, or_8_out, or_9_out, or_10_out;

  Decoder #(.select(3)) decoder_1 (
    .out0(decoder_1_out0), .out1(decoder_1_out1), .out2(decoder_1_out2), .out3(decoder_1_out3),
    .out4(decoder_1_out4), .out5(decoder_1_out5), .out6(decoder_1_out6), .out7(decoder_1_out7), .sel(ABC));  // open: en
  or c (c_out, decoder_1_out3, decoder_1_out4, decoder_1_out5);
  or or_1 (or_1_out, decoder_1_out1, decoder_1_out2, decoder_1_out3);
  or or_2 (or_2_out, decoder_1_out0, decoder_1_out1, decoder_1_out2);
  or f (f_out, decoder_1_out0, decoder_1_out1, decoder_1_out3);
  or or_3 (or_3_out, decoder_1_out0, decoder_1_out2, decoder_1_out3);
  or or_4 (or_4_out, decoder_1_out0, decoder_1_out2, decoder_1_out3);
  or or_5 (or_5_out, decoder_1_out0, decoder_1_out2, decoder_1_out4);
  or or_6 (or_6_out, or_1_out, decoder_1_out5);
  or or_7 (or_7_out, or_2_out, decoder_1_out3);
  or or_8 (or_8_out, or_3_out, decoder_1_out5);
  or or_9 (or_9_out, or_4_out, decoder_1_out4, decoder_1_out5);
  or or_10 (or_10_out, or_5_out, decoder_1_out5);
  _7_Segment_Display u_7_segment_display_1 (
    .g(or_8_out), .f(f_out), .a(or_9_out), .b(or_10_out), .e(or_7_out), .d(or_6_out), .c(c_out));  // open: dp

  // Notes on the sheet:
  //   Decoder
  //   a
  //   b
  //   d
  //   e
  //   g
endmodule

module _7_segment_MUX (
  input  C,
  input  [1:0] A_B
);

  wire multiplexer_1_out, multiplexer_2_out, multiplexer_3_out, multiplexer_4_out, multiplexer_5_out,
       multiplexer_6_out, multiplexer_7_out, not_1_out;

  not not_1 (not_1_out, C);
  Multiplexer #(.select(2)) multiplexer_1 (
    .in0(not_1_out), .in1(1'b1), .in2(1'b1), .out(multiplexer_1_out), .sel(A_B));  // open: in3, en
  Multiplexer #(.select(2)) multiplexer_2 (
    .in0(not_1_out), .in1(not_1_out), .in2(1'b1), .out(multiplexer_2_out), .sel(A_B));  // open: in3, en
  Multiplexer #(.select(2)) multiplexer_3 (
    .in0(1'b0), .in1(C), .in2(1'b1), .out(multiplexer_3_out), .sel(A_B));  // open: in3, en
  Multiplexer #(.select(2)) multiplexer_4 (
    .in0(C), .in1(1'b1), .in2(C), .out(multiplexer_4_out), .sel(A_B));  // open: in3, en
  Multiplexer #(.select(2)) multiplexer_5 (
    .in0(1'b1), .in1(1'b1), .in2(1'b0), .out(multiplexer_5_out), .sel(A_B));  // open: in3, en
  Multiplexer #(.select(2)) multiplexer_6 (
    .in0(1'b1), .in1(C), .in2(1'b0), .out(multiplexer_6_out), .sel(A_B));  // open: in3, en
  Multiplexer #(.select(2)) multiplexer_7 (
    .in0(not_1_out), .in1(1'b1), .in2(C), .out(multiplexer_7_out), .sel(A_B));  // open: in3, en
  _7_Segment_Display u_7_segment_display_1 (
    .g(multiplexer_7_out), .f(multiplexer_6_out), .a(multiplexer_1_out), .b(multiplexer_2_out),
    .e(multiplexer_5_out), .d(multiplexer_4_out), .c(multiplexer_3_out));  // open: dp

  // Notes on the sheet:
  //   a
  //   b
  //   c
  //   d
  //   e
  //   f
  //   g
  //   Multiplexer
endmodule

module flip_flop (
);

  wire and_1_out, and_2_out, and_3_out, and_4_out, and_5_out, clock_1_out, j_k_ff_1_q, j_k_ff_2_q,
       j_k_ff_3_q, not_1_out, not_2_out, not_3_out, or_1_out, or_2_out, or_3_out, or_4_out, or_5_out,
       or_6_out, or_7_out, or_8_out;

  not not_1 (not_1_out, j_k_ff_3_q);
  not not_2 (not_2_out, j_k_ff_2_q);
  not not_3 (not_3_out, j_k_ff_1_q);
  or or_1 (or_1_out, j_k_ff_3_q, j_k_ff_2_q, not_3_out);
  or or_2 (or_2_out, j_k_ff_3_q, not_3_out);
  or or_3 (or_3_out, j_k_ff_3_q, j_k_ff_2_q);
  or or_4 (or_4_out, j_k_ff_3_q, j_k_ff_1_q);
  or or_5 (or_5_out, j_k_ff_2_q, j_k_ff_1_q);
  and and_1 (and_1_out, not_1_out, not_1_out);
  or or_6 (or_6_out, not_2_out, j_k_ff_1_q);
  or or_7 (or_7_out, j_k_ff_3_q, j_k_ff_2_q, not_3_out);
  or or_8 (or_8_out, not_1_out, j_k_ff_1_q);
  and and_2 (and_2_out, or_3_out, or_4_out);
  and and_3 (and_3_out, not_1_out, or_6_out);
  and and_4 (and_4_out, or_7_out, or_8_out);
  _7_Segment_Display u_7_segment_display_1 (
    .g(and_4_out), .f(and_3_out), .a(or_1_out), .b(or_2_out), .e(and_1_out), .d(or_5_out), .c(and_2_out));  // open: dp
  Clock clock_1 (.out(clock_1_out));
  J_K_Flip_Flop j_k_ff_1 (.J(1'b1), .clk(clock_1_out), .K(1'b1), .Q(j_k_ff_1_q));  // open: Qn, preset, en, reset
  J_K_Flip_Flop j_k_ff_2 (
    .J(j_k_ff_1_q), .clk(clock_1_out), .K(j_k_ff_1_q), .Q(j_k_ff_2_q));  // open: Qn, preset, en, reset
  and and_5 (and_5_out, j_k_ff_1_q, j_k_ff_2_q);
  J_K_Flip_Flop j_k_ff_3 (
    .J(and_5_out), .clk(clock_1_out), .K(and_5_out), .Q(j_k_ff_3_q));  // open: Qn, preset, en, reset

  // Notes on the sheet:
  //   A
  //   B
  //   C
  //   a
  //   c
  //   d
  //   e
  //   f
  //   g
  //   Counter
endmodule
